# Fritzing sketch OdinSecurity (saved by Fritzing 0.9.3b)
breadboards: 1

parts:
  Componente1 = Arduino Uno (Rev3)
  PIR1 = PIR sensor
  PIR2 = PIR sensor
  J1 = Basic Servo
  J2 = Basic Servo
  Raspberry_Pi_1 = Raspberry Pi 3 [part_number=RPI-3-V1.2]  # not connected

nets:
  N1: Componente1.D12/MISO, PIR1.SIG
  N2: Componente1.D13/SCK, PIR2.SIG
  VDD: Componente1.5V, PIR1.VDD, PIR2.VDD, J1.vcc, J2.vcc
  GND: Componente1.GND, PIR1.GND, PIR2.GND, J1.gnd, J2.gnd
